# Fritzing sketch diagramaCircuitos (saved by Fritzing 0.9.3b)
breadboards: 1

parts:
  Componente1 = Arduino Uno (Rev3)
  J1 = Basic Servo
  J2 = Basic Servo
  LED1 = LED - 5mm [color="Red (633nm)" package="5 mm [THT]"]
  U3 = 2-Channel 5v Relay Shield [package=relay-2ch5v10a]
  YL-83_-_Control_Board1 = YL-83 Rain Sensor - Control Board
  YL-83_-_Detection_Board1 = YL-83 Rain Sensor - Detection Board
  BT1 = Bluetooth HC-06u [package=THT]
  Componente2 = FC-28 Soil Hygrometer Module - Probe
  Componente3 = FC-28 Soil Hygrometer Module
  DHT1 = DHT11 Humitidy and Temperature Sensor
  LCD1 = LCD screen
  LCM1602_IIC1 = LCM1602 IIC [part_number="LCM1602 IIC" chip_label="LCM1602 IIC" package="DIP (Dual Inline) [THT]"]
  R1 = Resistor [tolerance=±5% resistance=220 package=THT]
  Power_plug1 = Power plug
  M2 = DC Motor
  F1 = Fan - Ventilador [package=THT]

nets:
  N1: Componente1.A0, Componente3.AO
  N2: Componente1.A4/SDA, LCM1602_IIC1.SCL
  N3: Componente1.A5/SCL, LCM1602_IIC1.SDA
  N4: Componente1.D8, J2.pulse
  N5: Componente1.D12/MISO, U3.IN2
  N6: Componente1.D13/SCK, U3.IN1
  N7: Componente1.D0/RX, BT1.TXD
  N8: Componente1.D1/TX, BT1.RXD
  N9: Componente1.D2, DHT1.DATA
  N10: Componente1.D3_PWM, LED1.anode
  N11: Componente1.D4, YL-83_-_Control_Board1.DO
  N12: Componente1.D7, J1.pulse
  VCC: Componente1.5V, J1.vcc, J2.vcc, U3.VCC, YL-83_-_Control_Board1.VCC, BT1.VCC, Componente3.VCC, DHT1.VDD, LCM1602_IIC1.VCC
  GND: Componente1.GND, J1.gnd, J2.gnd, U3.GND, YL-83_-_Control_Board1.GND, BT1.GND, Componente3.GND, DHT1.GND, LCM1602_IIC1.GND, R1.Pin_1
  N13: LED1.cathode, R1.Pin_0
  N14: U3.K1-In, F1.5V
  N15: U3.K2-In, M2.pin_2
  N16: U3.K2-On, Power_plug1.VCC
  N17: YL-83_-_Control_Board1.POS, YL-83_-_Detection_Board1.POS
  N18: YL-83_-_Control_Board1.NEG, YL-83_-_Detection_Board1.NEG
  N19: Componente2.POS, Componente3.POS
  N20: Componente2.NEG, Componente3.NEG
  VSS: LCD1.VSS, LCM1602_IIC1.VSS
  VDD: LCD1.VDD, LCM1602_IIC1.VDD
  N21: LCD1.V0, LCM1602_IIC1.V0
  N22: LCD1.RS, LCM1602_IIC1.RS
  N23: LCD1.R/W, LCM1602_IIC1.RW
  N24: LCD1.E, LCM1602_IIC1.E
  N25: LCD1.DB0, LCM1602_IIC1.D0
  N26: LCD1.DB1, LCM1602_IIC1.D1
  N27: LCD1.DB2, LCM1602_IIC1.D2
  N28: LCD1.DB3, LCM1602_IIC1.D3
  N29: LCD1.DB4, LCM1602_IIC1.D4
  N30: LCD1.DB5, LCM1602_IIC1.D5
  N31: LCD1.DB6, LCM1602_IIC1.D6
  N32: LCD1.DB7, LCM1602_IIC1.D7
  N33: LCD1.LED+, LCM1602_IIC1.A
  N34: LCD1.LED-, LCM1602_IIC1.K
  N35: Power_plug1.GND, M2.pin_1

notes:
  Bomba de agua
  Fuente 220v o 12v
  modulo bluetooth hc-06
  Servo 1
  Servo 2

custom parts:
  2-Channel 5v Relay Shield: 2 Channel 5v Relay Shield w. 2x SPD-06VDC-SD-C
  YL-83 Rain Sensor - Control Board: The YL-83 is a rain sensor that has more resistance when dry and less resistance when wet. The module runs at 5V.
  YL-83 Rain Sensor - Detection Board: The YL-83 is a rain sensor that has more resistance when dry and less resistance when wet. The module runs at 5V.
  Bluetooth HC-06u: Bluetooth HC-06 - face up, pins down 16.5mm x 37.5mm PCB
  FC-28 Soil Hygrometer Module - Probe: The FC-28 is a soil hygrometer module that uses the Texas Instruments LM393 comparator chip to provide an analog measurement of soil humidity.
  FC-28 Soil Hygrometer Module: The FC-28 is a soil hygrometer module that uses the Texas Instruments LM393 comparator chip to provide an analog measurement of soil humidity. The digital output is high when soil moisture is over a certain threshold, as determined by adjusting the potentiometer.
  DHT11 Humitidy and Temperature Sensor: DHT11 Humidity and Temperature Sensor
  LCM1602 IIC: I2C-Module to use a 1602 or 2004 LCD on with the wire.h libory Serial LCD Modul
  Fan - Ventilador: Ventilador de 2 pines, se encuentra comunmente en computadoras de escritorio
